// Logisim project lab6_template.circ as structural Verilog: 6 circuits, main circuit main
module main (
  input  clk
);

  wire [11:0] pc_update_1_pc, undriven;

  // Probe on undriven
  fetch fetch_1 (.pc(undriven));  // open: icode, ifun, rA, rB, valC, valP
  decode decode_1 ();  // open: rA, rB, icode, M, E, clk, valA, valB
  execute execute_1 ();  // open: icode, ifun, valA, valC, valB, clk, valE, cnd
  memory memory_1 ();  // open: icode, valA, valE, clk, valP, valM
  pc_update pc_update_1 (.PC(pc_update_1_pc));  // open: cnd, icode, valC, valM, valP
  Register #(.width(12)) newPC (.D(pc_update_1_pc));  // open: en, Q, clk, clr

  // Notes on the sheet:
  //   * this is a probe. it is not an input. it only shows you the value in a wire
  //   Fetch
  //   Decode
  //   Execute
  //   Write Back
  //   * not a subcircuit, but still an important part of the CPU. 
  //   Memory
  //   PC Update
endmodule

module fetch (
  input  [11:0] pc,
  output [3:0] icode,
  output [3:0] ifun,
  output [3:0] rA,
  output [3:0] rB,
  output [63:0] valC,
  output [11:0] valP
);


  // Notes on the sheet:
  //   * fetch needs a ROM. I implemented this using two ROMs, but i'll let you figure out if that is necessary for your implementation
endmodule

module decode (
  input  [3:0] rA,
  input  [3:0] rB,
  input  [3:0] icode,
  input  [63:0] M,
  input  [63:0] E,
  input  clk,
  output [63:0] valA,
  output [63:0] valB
);


  // Notes on the sheet:
  //   clk is not necessary to read from the registers
  //   Note that clk should only be active during the write back stage
  //   you will have to figure out how to do this. I suggest using a stage counter in main and using that to determine whether or not to send the clock signal to decode
endmodule

module execute (
  input  [3:0] icode,
  input  [3:0] ifun,
  input  [63:0] valA,
  input  [63:0] valC,
  input  [63:0] valB,
  input  clk,
  output cnd,
  output [63:0] valE
);
endmodule

module memory (
  input  [3:0] icode,
  input  [63:0] valA,
  input  [63:0] valE,
  input  [11:0] valP,
  input  clk,
  output [63:0] valM
);


  // Notes on the sheet:
  //   * memory needs a RAM (obviously). you can figure out how to set that up
endmodule

module pc_update (
  input  [3:0] icode,
  input  cnd,
  input  [63:0] valC,
  input  [63:0] valM,
  input  [11:0] valP,
  output [11:0] PC
);
endmodule
