// Logisim project main.circ as structural Verilog: 6 circuits, main circuit main
module main (
  input  clk
);

  wire clock_1_out, undriven;
  wire [11:0] fetch_1_valp, pc_update_1_pc, register_1_q;

  Clock clock_1 (.out(clock_1_out));
  // Probe on undriven
  Register #(.width(12)) register_1 (
    .D(fetch_1_valp), .en(clock_1_out), .clk(clock_1_out), .Q(register_1_q));  // open: clr
  fetch fetch_1 (.pc(register_1_q), .valP(fetch_1_valp));  // open: icode, ifun, valC, rB, rA
  decode decode_1 ();  // open: rA, rB, icode, M, E, clk, valA, valB
  execute execute_1 ();  // open: icode, ifun, valA, valC, valB, clk, valE, cnd
  memory memory_1 ();  // open: icode, valA, valE, clk, valP, valM
  pc_update pc_update_1 (.PC(pc_update_1_pc));  // open: cnd, icode, valC, valM, valP
  Register #(.width(12)) newPC (.D(pc_update_1_pc));  // open: en, Q, clk, clr

  // Notes on the sheet:
  //   * this is a probe. it is not an input. it only shows you the value in a wire
  //   Fetch
  //   Decode
  //   Execute
  //   Write Back
  //   * not a subcircuit, but still an important part of the CPU. 
  //   Memory
  //   PC Update
endmodule

module fetch (
  input  [11:0] pc,
  output [3:0] icode,
  output [3:0] ifun,
  output [3:0] rB,
  output [3:0] rA,
  output [63:0] valC,
  output [11:0] valP
);

  wire adder_1_cout, adder_2_cout;
  wire [1:0] byte_offsets_do_not_edit_data;
  wire [3:0] and_1_out, multiplexer_3_out;
  wire [3:3] or_1_out;
  wire [7:0] code_p3, undriven;
  wire [11:0] rom_1_p1;
  wire [55:0] undriven_2;

  // NoConnect on adder_1_cout
  // ROM #(.addrWidth(12), .line("dual"), .misaligned("true")) code: pin names not known; wires that end beside it: 12'h1e, pc, code_p3
  // ROM #(.addrWidth(12), .line("octo"), .misaligned("true")) rom_1: pin names not known; wires that end beside it: rom_1_p1
  Adder #(.width(12)) adder_1 (.a(pc), .b(12'h2), .out(rom_1_p1), .cin(1'b0), .cout(adder_1_cout));
  ROM #(.addrWidth(4), .dataWidth(2)) byte_offsets_do_not_edit (.addr(icode), .data(byte_offsets_do_not_edit_data));
  Multiplexer #(.select(2), .width(8)) multiplexer_1 (
    .in0({8{1'b0}}), .in1(code_p3), .in2({8{1'b0}}), .in3(code_p3), .out({rA, rB}),
    .sel(byte_offsets_do_not_edit_data));
  Multiplexer #(.select(2), .width(64)) multiplexer_2 (
    .in0({64{1'b0}}), .in1({64{1'b0}}), .in2({undriven_2, code_p3}), .in3({undriven, undriven_2}),
    .out(valC), .sel(byte_offsets_do_not_edit_data));
  Multiplexer #(.select(2), .width(4)) multiplexer_3 (
    .in0(4'b0001), .in1(4'b0010), .in2(4'b1001), .in3(4'b1010), .out(multiplexer_3_out),
    .sel(byte_offsets_do_not_edit_data));
  or or_1 (or_1_out[3], icode[0], icode[1], icode[2], icode[3]);
  assign and_1_out = {4{or_1_out[3]}} & multiplexer_3_out;  // AND_Gate and_1, 4 bits wide
  // NoConnect on adder_2_cout
  Adder #(.width(12)) adder_2 (.a({{8{1'b0}}, and_1_out}), .b(pc), .out(valP), .cout(adder_2_cout));  // open: cin

  // Notes on the sheet:
  //   contents of code (hex, n*v repeats v):
  //   30 f4 0 1 6*0 30 f0 f 7*0 30 f1 a 7*0 20 2 60 12 20 28 20 2 61 12 20 29 20 2 a0 2f b0 3f
  //   contents of rom_1 (hex, n*v repeats v):
  //   30 f4 0 1 6*0 30 f0 f 7*0 30 f1 a 7*0 20 2 60 12 20 28 20 2 61 12 20 29 20 2 a0 2f b0 3f
  //   first 2 ROM bytes (Set me)
  //   last 8 ROM bytes (Set same val)
  //   8-15 vals?
  //   0-7, icode ifun
  //   contents of byte_offsets_do_not_edit (hex, n*v repeats v):
  //   0 0 1 3 3 3 1 2 2 0 1 1
  //   00 = no args +0
  //   01 = rA:rB +1
  //   10 = V/D +8
  //   11 = rA:rB + V/D +9
  //   Do not edit^ Byte Offsets encoded
  //   10 = V/D -> bytes 1-8
  //   11 = rA:rB + V/D -> bytes 2-9
  //   PC + 00: +1, 01: +2, 10: +9, 11: +10
  //   << HALT (0x00) overrides +PC to 0
endmodule

module decode (
  input  [3:0] rA,
  input  [3:0] rB,
  input  [3:0] icode,
  input  [63:0] M,
  input  [63:0] E,
  input  clk,
  output [63:0] valA,
  output [63:0] valB
);


  // Notes on the sheet:
  //   clk is not necessary to read from the registers
  //   Note that clk should only be active during the write back stage
  //   you will have to figure out how to do this. I suggest using a stage counter in main and using that to determine whether or not to send the clock signal to decode
endmodule

module execute (
  input  [3:0] icode,
  input  [3:0] ifun,
  input  [63:0] valA,
  input  [63:0] valC,
  input  [63:0] valB,
  input  clk,
  output cnd,
  output [63:0] valE
);
endmodule

module memory (
  input  [3:0] icode,
  input  [63:0] valA,
  input  [63:0] valE,
  input  [11:0] valP,
  input  clk,
  output [63:0] valM
);


  // Notes on the sheet:
  //   * memory needs a RAM (obviously). you can figure out how to set that up
endmodule

module pc_update (
  input  [3:0] icode,
  input  cnd,
  input  [63:0] valC,
  input  [63:0] valM,
  input  [11:0] valP,
  output [11:0] PC
);
endmodule
